# Fritzing sketch uart (saved by Fritzing 0.9.3b)
breadboards: 1

parts:
  Raspberry_Pi_1 = Raspberry Pi 3 [part_number=RPI-3-V1.2]
  Part1 = Adafruit Ultimate GPS v3 [part_number="Adafruit #746"]
  Part2 = Adafruit BME280

nets:
  3V3: Raspberry_Pi_1.3v3, Raspberry_Pi_1.3V3, Part1.3.3V, Part2.3.3V
  N1: Raspberry_Pi_1.GPIO2, Part2.SDI/SDA
  N2: Raspberry_Pi_1.GPIO3, Part2.SCK/SCL
  GND: Raspberry_Pi_1.GND, Part1.GND, Part2.GND
  N3: Raspberry_Pi_1.GIPO15, Part1.TX
  N4: Raspberry_Pi_1.GIPO14, Part1.RX

custom parts:
  Adafruit Ultimate GPS v3: We carry a few different GPS modules here in the Adafruit shop, but none that satisfied our every desire - that's why we designed this little GPS breakout board. We believe this is the Ultimate GPS module, so we named it that. It's got everything you want and more: -165 dBm sensitivity, 10 Hz updates, 66 channels 5V friendly design and only 20mA current draw Breadboard friendly + two mounting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
  Adafruit BME280: Bosch has stepped up their game with their new BME280 sensor, an environmental sensor with temperature, barometric pressure and humidity! This sensor is great for all sorts of weather/environmental sensing and can even be used in both I2C and SPI! This precision sensor from Bosch is the best low-cost sensing solution for measuring humidity with ±3% accuracy, barometric pressure with ±1 hPa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
